// Logisim project B100_ALU.circ as structural Verilog: 1 circuit, main circuit main
module main (
  input  [15:0] Instructions,
  input  [15:0] Direct_Value,
  input  [15:0] DATA,
  input  [15:0] DATA_2,
  output [15:0] Output,
  output out_6,
  output out_7,
  output [15:0] Output_2,
  output out_9
);

  wire button_1_out, button_2_out, Clock_2_out, Clock_out, not_1_out;
  wire [15:0] A_q, adder_1_out, and_1_out, B_q, controlled_buffer_1_out, not_2_out, not_3_out, or_1_out,
       ram_1_data, ram_2_data, subtractor_1_out;

  Button Clock (.out(Clock_out));
  Button Clock_2 (.out(Clock_2_out));
  RAM #(.addrWidth(6), .dataWidth(16), .bus("separate")) ram_1 (
    .addr(Instructions[5:0]), .din(DATA), .data(ram_1_data), .sel(1'b1), .clk(Clock_out), .ld(1'b1));  // open: str, clr
  RAM #(.addrWidth(6), .dataWidth(16), .bus("separate")) ram_2 (
    .addr(Instructions[11:6]), .din(DATA_2), .data(ram_2_data), .sel(1'b1), .clk(Clock_2_out), .ld(1'b1));  // open: str, clr
  Register #(.width(16)) A (.D(ram_1_data), .en(1'b1), .Q(A_q), .clk(button_1_out));  // open: clr
  Button button_1 (.out(button_1_out));
  Register #(.width(16)) B (.D(ram_2_data), .en(1'b1), .Q(B_q), .clk(button_2_out));  // open: clr
  Button button_2 (.out(button_2_out));
  not not_1 (not_1_out, Instructions[15]);
  assign controlled_buffer_1_out = not_1_out ? Direct_Value : 16'bz;  // Controlled_Buffer controlled_buffer_1
  Adder #(.width(16)) adder_1 (.a(A_q), .b(B_q), .out(adder_1_out), .cout(out_7));  // open: cin
  Subtractor #(.width(16)) subtractor_1 (.a(A_q), .b(B_q), .out(subtractor_1_out), .bout(out_9));  // open: bin
  assign not_2_out = ~A_q;  // NOT_Gate not_2, 16 bits wide
  assign not_3_out = ~B_q;  // NOT_Gate not_3, 16 bits wide
  Adder #(.width(16)) adder_2 (.a(A_q), .b(controlled_buffer_1_out), .out(Output), .cout(out_6));  // open: cin
  assign or_1_out = A_q | B_q;  // OR_Gate or_1, 16 bits wide
  assign and_1_out = A_q & B_q;  // AND_Gate and_1, 16 bits wide
  Multiplexer #(.select(3), .width(16)) multiplexer_1 (
    .in0(adder_1_out), .in1(subtractor_1_out), .in2(or_1_out), .in3(and_1_out), .in4(not_2_out),
    .in5(not_3_out), .out(Output_2), .sel(Instructions[14:12]), .en(Instructions[15]));  // open: in6, in7

  // Notes on the sheet:
  //   Operator
  //   Spiltter
  //   B
  //   Addre
  //    Addre A
  //   A or B
  //   A and B
  //   Not A
  //   Not b
endmodule
