// Logisim project 1-bit Full Adder.circ as structural Verilog: 1 circuit, main circuit main
module main (
  input  x0,
  input  x1,
  input  S,
  input  Cin,
  input  Cout
);

  wire and_1_out, and_2_out, or_1_out, xor_1_out, xor_2_out;

  xor xor_1 (xor_1_out, x0, x1);
  xor xor_2 (xor_2_out, xor_1_out, Cin);
  and and_1 (and_1_out, Cin, xor_1_out);
  and and_2 (and_2_out, x1, x0);
  or or_1 (or_1_out, and_1_out, and_2_out);
endmodule
