// Logisim project 1-bit Full Subtractor.circ as structural Verilog: 1 circuit, main circuit main
module main (
  input  Cin,
  input  x0,
  input  Diff,
  input  x1,
  input  Borrow
);

  wire and_1_out, and_2_out, not_1_out, not_2_out, xor_1_out, xor_2_out;

  not not_1 (not_1_out, x0);
  xor xor_1 (xor_1_out, x0, x1);
  and and_1 (and_1_out, x1, not_1_out);
  not not_2 (not_2_out, xor_1_out);
  xor xor_2 (xor_2_out, Cin, xor_1_out);
  and and_2 (and_2_out, not_2_out, Cin);
  or or_1 (Borrow, and_2_out, and_1_out);
endmodule
