// Logisim project 1-bit Half Adder.circ as structural Verilog: 1 circuit, main circuit main
module main (
  input  X0,
  input  S,
  input  X1,
  input  C
);

  wire and_1_out, xor_1_out;

  xor xor_1 (xor_1_out, X0, X1);
  and and_1 (and_1_out, X0, X1);
endmodule
