// Logisim project 1-bit Half Subtractor.circ as structural Verilog: 1 circuit, main circuit main
module main (
  input  X0,
  input  X1
);

  wire and_1_out, not_1_out, xor_1_out;

  not not_1 (not_1_out, X0);
  xor xor_1 (xor_1_out, X0, X1);
  and and_1 (and_1_out, X1, not_1_out);

  // Notes on the sheet:
  //   DIFF
  //   BORROW
endmodule
