// Logisim project 2 bit full adder.circ as structural Verilog: 1 circuit, main circuit main
module main (
  input  in_1,
  input  in_2,
  input  in_3,
  input  in_4,
  input  in_5,
  input  in_6
);

  wire and_1_out, and_2_out, and_3_out, and_4_out, or_1_out, or_2_out, undriven, xor_1_out, xor_2_out,
       xor_4_out;

  xor xor_1 (xor_1_out, in_1, in_2);
  xor xor_2 (xor_2_out, in_3, in_4);
  // XOR_Gate xor_3 has open pins: in1=xor_1_out, in3=undriven, out=open
  and and_1 (and_1_out, or_1_out, xor_2_out);
  and and_2 (and_2_out, in_4, in_3);
  and and_3 (and_3_out, xor_1_out, undriven);
  and and_4 (and_4_out, in_2, in_1);
  xor xor_4 (xor_4_out, xor_2_out, or_1_out);
  or or_1 (or_1_out, and_3_out, and_4_out);
  or or_2 (or_2_out, and_1_out, and_2_out);
endmodule
