// Logisim project 2 bit full subtractor.circ as structural Verilog: 1 circuit, main circuit main
module main (
  input  C_in,
  input  x0,
  input  x1,
  output D,
  output C
);

  wire and_1_out, and_2_out, not_1_out, not_2_out, xor_1_out;

  not not_1 (not_1_out, x0);
  xor xor_1 (xor_1_out, x0, x1);
  and and_1 (and_1_out, not_1_out, x0);
  not not_2 (not_2_out, xor_1_out);
  and and_2 (and_2_out, not_2_out, C_in);
  xor xor_2 (D, xor_1_out, C_in);
  or or_1 (C, and_2_out, and_1_out);
endmodule
