// Logisim project 8bit_adder.circ as structural Verilog: 1 circuit, main circuit main
module main (
  input  A1,
  input  A1_2,
  input  B1,
  input  B1_2,
  input  C_in,
  input  A2,
  input  A2_2,
  input  B2,
  input  B2_2,
  input  A3,
  input  A3_2,
  input  B3,
  input  B3_2,
  input  A4,
  input  A4_2,
  input  B4,
  input  B4_2,
  output S1,
  output S1_2,
  output S2,
  output S2_2,
  output S3,
  output S3_2,
  output S4,
  output S4_2,
  output C_out
);

  wire and_1_out, and_2_out, and_3_out, and_4_out, and_5_out, and_6_out, and_7_out, and_8_out, and_9_out,
       and_10_out, and_11_out, and_12_out, and_13_out, and_14_out, and_15_out, and_16_out, or_1_out,
       or_2_out, or_3_out, or_4_out, or_5_out, or_6_out, or_7_out, xor_1_out, xor_2_out, xor_3_out,
       xor_4_out, xor_9_out, xor_10_out, xor_11_out, xor_12_out;

  xor xor_1 (xor_1_out, A1, B1);
  xor xor_2 (xor_2_out, A2, B2);
  xor xor_3 (xor_3_out, A3, B3);
  xor xor_4 (xor_4_out, A4, B4);
  xor xor_5 (S1, xor_1_out, C_in);
  and and_1 (and_1_out, C_in, xor_1_out);
  buf and_2 (and_2_out, B1);  // AND_Gate
  xor xor_6 (S2, xor_2_out, or_2_out);
  and and_3 (and_3_out, or_2_out, xor_2_out);
  and and_4 (and_4_out, B2, A2);
  xor xor_7 (S3, xor_3_out, or_1_out);
  and and_5 (and_5_out, or_1_out, xor_3_out);
  and and_6 (and_6_out, B3, A3);
  xor xor_8 (S4, xor_4_out, or_3_out);
  and and_7 (and_7_out, or_3_out, xor_4_out);
  and and_8 (and_8_out, B4, A4);
  or or_1 (or_1_out, and_3_out, and_4_out);
  or or_2 (or_2_out, and_1_out, and_2_out);
  or or_3 (or_3_out, and_5_out, and_6_out);
  or or_4 (or_4_out, and_7_out, and_8_out);
  xor xor_9 (xor_9_out, A1_2, B1_2);
  xor xor_10 (xor_10_out, A2_2, B2_2);
  xor xor_11 (xor_11_out, A3_2, B3_2);
  xor xor_12 (xor_12_out, A4_2, B4_2);
  xor xor_13 (S1_2, xor_9_out, or_4_out);
  and and_9 (and_9_out, or_4_out, xor_9_out);
  and and_10 (and_10_out, B1_2, A1_2);
  xor xor_14 (S2_2, xor_10_out, or_5_out);
  and and_11 (and_11_out, or_5_out, xor_10_out);
  and and_12 (and_12_out, B2_2, A2_2);
  xor xor_15 (S3_2, xor_11_out, or_6_out);
  and and_13 (and_13_out, or_6_out, xor_11_out);
  and and_14 (and_14_out, B3_2, A3_2);
  xor xor_16 (S4_2, xor_12_out, or_7_out);
  and and_15 (and_15_out, or_7_out, xor_12_out);
  and and_16 (and_16_out, B4_2, A4_2);
  or or_5 (or_5_out, and_9_out, and_10_out);
  or or_6 (or_6_out, and_11_out, and_12_out);
  or or_7 (or_7_out, and_13_out, and_14_out);
  or or_8 (C_out, and_15_out, and_16_out);
endmodule
