// Logisim project 8bit_subtractor.circ as structural Verilog: 1 circuit, main circuit main
module main (
  input  A1,
  input  A5,
  input  B1,
  input  B5,
  input  C_in,
  input  A2,
  input  A6,
  input  B2,
  input  B6,
  input  A3,
  input  A7,
  input  B3,
  input  B7,
  input  A4,
  input  A8,
  input  B4,
  input  B8,
  output D1,
  output D5,
  output D2,
  output D6,
  output D3,
  output D7,
  output D4,
  output D8,
  output C_out
);

  wire and_1_out, and_2_out, and_3_out, and_4_out, and_5_out, and_6_out, and_7_out, and_8_out, and_9_out,
       and_10_out, and_11_out, and_12_out, and_13_out, and_14_out, and_15_out, and_16_out, not_1_out,
       not_2_out, not_3_out, not_4_out, not_5_out, not_6_out, not_7_out, not_8_out, not_9_out, not_10_out,
       not_11_out, not_12_out, not_13_out, not_14_out, not_15_out, not_16_out, or_1_out, or_2_out, or_3_out,
       or_4_out, or_5_out, or_6_out, or_7_out, xor_1_out, xor_2_out, xor_3_out, xor_4_out, xor_9_out,
       xor_10_out, xor_11_out, xor_12_out;

  not not_1 (not_1_out, B1);
  not not_2 (not_2_out, B2);
  not not_3 (not_3_out, B3);
  not not_4 (not_4_out, B4);
  xor xor_1 (xor_1_out, B1, C_in);
  and and_1 (and_1_out, not_1_out, C_in);
  xor xor_2 (xor_2_out, B2, or_1_out);
  and and_2 (and_2_out, not_2_out, or_1_out);
  xor xor_3 (xor_3_out, B3, or_2_out);
  and and_3 (and_3_out, not_3_out, or_2_out);
  xor xor_4 (xor_4_out, B4, or_3_out);
  and and_4 (and_4_out, not_4_out, or_3_out);
  not not_5 (not_5_out, xor_1_out);
  not not_6 (not_6_out, xor_2_out);
  not not_7 (not_7_out, xor_3_out);
  not not_8 (not_8_out, xor_4_out);
  xor xor_5 (D1, A1, xor_1_out);
  xor xor_6 (D2, A2, xor_2_out);
  xor xor_7 (D3, A3, xor_3_out);
  xor xor_8 (D4, A4, xor_4_out);
  and and_5 (and_5_out, not_5_out, A1);
  and and_6 (and_6_out, not_6_out, A2);
  and and_7 (and_7_out, not_7_out, A3);
  and and_8 (and_8_out, not_8_out, A4);
  or or_1 (or_1_out, and_5_out, and_1_out);
  or or_2 (or_2_out, and_6_out, and_2_out);
  or or_3 (or_3_out, and_7_out, and_3_out);
  or or_4 (or_4_out, and_8_out, and_4_out);
  xor xor_9 (xor_9_out, B5, or_4_out);
  not not_9 (not_9_out, B5);
  xor xor_10 (xor_10_out, B6, or_5_out);
  not not_10 (not_10_out, B6);
  xor xor_11 (xor_11_out, B7, or_6_out);
  not not_11 (not_11_out, B7);
  xor xor_12 (xor_12_out, B8, or_7_out);
  not not_12 (not_12_out, B8);
  and and_9 (and_9_out, not_9_out, or_4_out);
  and and_10 (and_10_out, not_10_out, or_5_out);
  and and_11 (and_11_out, not_11_out, or_6_out);
  and and_12 (and_12_out, not_12_out, or_7_out);
  xor xor_13 (D5, A5, xor_9_out);
  not not_13 (not_13_out, xor_9_out);
  xor xor_14 (D6, A6, xor_10_out);
  not not_14 (not_14_out, xor_10_out);
  xor xor_15 (D7, A7, xor_11_out);
  not not_15 (not_15_out, xor_11_out);
  xor xor_16 (D8, A8, xor_12_out);
  not not_16 (not_16_out, xor_12_out);
  and and_13 (and_13_out, not_13_out, A5);
  and and_14 (and_14_out, not_14_out, A6);
  and and_15 (and_15_out, not_15_out, A7);
  and and_16 (and_16_out, not_16_out, A8);
  or or_5 (or_5_out, and_13_out, and_9_out);
  or or_6 (or_6_out, and_14_out, and_10_out);
  or or_7 (or_7_out, and_15_out, and_11_out);
  or or_8 (C_out, and_16_out, and_12_out);
endmodule
